# Fritzing sketch PKE_Metere (saved by Fritzing 0.9.3b)
breadboards: 3

parts:
  Part1 = Arduino Nano (Rev3.0)
  MP1584EN_Board1 = MP1584EN Power Regulator Board [part_number=MP1584EN]
  VCC1 = 4 x AAA Battery Mount
  Squix1 = OLED 0.96" 128x64 I2C SSD1306
  J1 = Basic Servo
  S1 = Pushbutton [package="[SMD]"]
  S2 = Pushbutton [package="[SMD]"]
  R1 = Resistor [tolerance=±5% resistance=220 package="2010 [SMD]"]
  R2 = Resistor [tolerance=±5% resistance=220 package="2010 [SMD]"]
  R3 = Resistor [tolerance=±5% resistance=220 package="2010 [SMD]"]
  R5 = Resistor [tolerance=±5% resistance=220 package="2010 [SMD]"]
  R6 = Resistor [tolerance=±5% resistance=220 package="2010 [SMD]"]
  R7 = Resistor [tolerance=±5% resistance=220 package="2010 [SMD]"]
  J2 = Piezo Speaker
  R8 = Resistor [tolerance=±5% resistance=220 package="2010 [SMD]"]
  D1 = LTE-302 [package=lte-302]
  D2 = LTE-302 [package=lte-302]
  D3 = LTE-302 [package=lte-302]
  D4 = LTE-302 [package=lte-302]
  D5 = LTE-302 [package=lte-302]
  D6 = LTE-302 [package=lte-302]
  R9 = Resistor [tolerance=±5% resistance=220 package="2010 [SMD]"]
  D7 = LTE-302 [package=lte-302]

nets:
  GND: Part1.GND, MP1584EN_Board1.OUT_-, Squix1.GND, J1.gnd, S1.Pin_1, S1.Pin_2, S2.Pin_3, S2.Pin_4, J2.pin1, D1.A, D2.A, D3.A, D4.A, D5.A, D6.A, D7.A
  N1: Part1.D3, S2.Pin_1, S2.Pin_2
  N2: Part1.D4, S1.Pin_3, S1.Pin_4
  N3: Part1.D5, R8.Pin_0
  N4: Part1.D6, R7.Pin_1
  N5: Part1.D7, R6.Pin_1
  N6: Part1.D8, R5.Pin_1
  N7: Part1.D9, R9.Pin_1
  N8: Part1.D10, R3.Pin_0
  N9: Part1.D11/MOSI, R2.Pin_0
  N10: Part1.D12/MISO, R1.Pin_0
  VCC: Part1.5V, MP1584EN_Board1.OUT_+, Squix1.VCC, J1.vcc
  N11: Part1.A5, Squix1.SCL
  N12: Part1.A4, Squix1.SCA
  N13: Part1.D13/SCK, J1.pulse
  N14: MP1584EN_Board1.IN_-, VCC1.-
  N15: MP1584EN_Board1.IN_+, VCC1.+
  N16: R1.Pin_1, D1.C
  N17: R2.Pin_1, D2.C
  N18: R3.Pin_1, D3.C
  N19: R5.Pin_0, D5.C
  N20: R6.Pin_0, D6.C
  N21: R7.Pin_0, D7.C
  N22: J2.pin2, R8.Pin_1
  N23: D4.C, R9.Pin_0

custom parts:
  MP1584EN Power Regulator Board: The MP1584EN is a high frequency step-down switching regulator. The input voltage range is 4.5V to 28V. The output voltage is set by the board's potentiometer.
